// Digital circuit 7 seg diode decode CA.dig as structural Verilog
module _7_seg_diode_decode_CA (
  input  ndp,
  input  A_2,
  input  C_2,
  input  B_2,
  input  D_2,
  input  nG1,
  input  nG2,
  output G,
  output F,
  output E,
  output D,
  output C,
  output B,
  output A,
  output dp
);

  wire _74154_1_p9, _74154_1_p10, _74154_1_p11, _74154_1_p12, _74154_1_p13, _74154_1_p14, _74154_1_p15,
       _74154_1_p16, _74154_1_p17, _74154_1_p18, _74154_1_p19, _74154_1_p20, _74154_1_p21, _74154_1_p22,
       _74154_1_p23, _74154_1_p24;

  // _74154 _74154_1: pin names not known; wires that end beside it: 1'b1, 1'b0, nG1, nG2, A_2, B_2, C_2, D_2, _74154_1_p9, _74154_1_p10, _74154_1_p11, _74154_1_p12, _74154_1_p13, _74154_1_p14, _74154_1_p15, _74154_1_p16, _74154_1_p17, _74154_1_p18, _74154_1_p19, _74154_1_p20, _74154_1_p21, _74154_1_p22, _74154_1_p23, _74154_1_p24
  PullUp pullup_1 (.out(dp));
  DiodeBackward diodebackward_1 (.in(_74154_1_p9), .out(A));
  DiodeBackward diodebackward_2 (.in(_74154_1_p11), .out(A));
  DiodeBackward diodebackward_3 (.in(_74154_1_p12), .out(A));
  DiodeBackward diodebackward_4 (.in(_74154_1_p14), .out(A));
  DiodeBackward diodebackward_5 (.in(_74154_1_p15), .out(A));
  DiodeBackward diodebackward_6 (.in(_74154_1_p16), .out(A));
  DiodeBackward diodebackward_7 (.in(_74154_1_p17), .out(A));
  DiodeBackward diodebackward_8 (.in(_74154_1_p18), .out(A));
  DiodeBackward diodebackward_9 (.in(_74154_1_p19), .out(A));
  DiodeBackward diodebackward_10 (.in(_74154_1_p21), .out(A));
  DiodeBackward diodebackward_11 (.in(_74154_1_p23), .out(A));
  DiodeBackward diodebackward_12 (.in(_74154_1_p24), .out(A));
  DiodeBackward diodebackward_13 (.in(ndp), .out(dp));
  PullUp pullup_2 (.out(A));
  PullUp pullup_3 (.out(B));
  DiodeBackward diodebackward_14 (.in(_74154_1_p9), .out(B));
  DiodeBackward diodebackward_15 (.in(_74154_1_p10), .out(B));
  DiodeBackward diodebackward_16 (.in(_74154_1_p11), .out(B));
  DiodeBackward diodebackward_17 (.in(_74154_1_p12), .out(B));
  DiodeBackward diodebackward_18 (.in(_74154_1_p13), .out(B));
  DiodeBackward diodebackward_19 (.in(_74154_1_p16), .out(B));
  DiodeBackward diodebackward_20 (.in(_74154_1_p17), .out(B));
  DiodeBackward diodebackward_21 (.in(_74154_1_p18), .out(B));
  DiodeBackward diodebackward_22 (.in(_74154_1_p19), .out(B));
  DiodeBackward diodebackward_23 (.in(_74154_1_p22), .out(B));
  PullUp pullup_4 (.out(C));
  DiodeBackward diodebackward_24 (.in(_74154_1_p9), .out(C));
  DiodeBackward diodebackward_25 (.in(_74154_1_p10), .out(C));
  DiodeBackward diodebackward_26 (.in(_74154_1_p12), .out(C));
  DiodeBackward diodebackward_27 (.in(_74154_1_p13), .out(C));
  DiodeBackward diodebackward_28 (.in(_74154_1_p14), .out(C));
  DiodeBackward diodebackward_29 (.in(_74154_1_p15), .out(C));
  DiodeBackward diodebackward_30 (.in(_74154_1_p16), .out(C));
  DiodeBackward diodebackward_31 (.in(_74154_1_p17), .out(C));
  DiodeBackward diodebackward_32 (.in(_74154_1_p18), .out(C));
  DiodeBackward diodebackward_33 (.in(_74154_1_p19), .out(C));
  DiodeBackward diodebackward_34 (.in(_74154_1_p20), .out(C));
  DiodeBackward diodebackward_35 (.in(_74154_1_p22), .out(C));
  PullUp pullup_5 (.out(D));
  DiodeBackward diodebackward_36 (.in(_74154_1_p9), .out(D));
  DiodeBackward diodebackward_37 (.in(_74154_1_p9), .out(E));
  DiodeBackward diodebackward_38 (.in(_74154_1_p11), .out(D));
  DiodeBackward diodebackward_39 (.in(_74154_1_p11), .out(E));
  DiodeBackward diodebackward_40 (.in(_74154_1_p12), .out(D));
  DiodeBackward diodebackward_41 (.in(_74154_1_p14), .out(D));
  DiodeBackward diodebackward_42 (.in(_74154_1_p15), .out(E));
  DiodeBackward diodebackward_43 (.in(_74154_1_p15), .out(D));
  DiodeBackward diodebackward_44 (.in(_74154_1_p17), .out(D));
  DiodeBackward diodebackward_45 (.in(_74154_1_p17), .out(E));
  DiodeBackward diodebackward_46 (.in(_74154_1_p18), .out(D));
  DiodeBackward diodebackward_47 (.in(_74154_1_p19), .out(E));
  DiodeBackward diodebackward_48 (.in(_74154_1_p20), .out(D));
  DiodeBackward diodebackward_49 (.in(_74154_1_p20), .out(E));
  DiodeBackward diodebackward_50 (.in(_74154_1_p21), .out(D));
  DiodeBackward diodebackward_51 (.in(_74154_1_p21), .out(E));
  DiodeBackward diodebackward_52 (.in(_74154_1_p22), .out(D));
  DiodeBackward diodebackward_53 (.in(_74154_1_p22), .out(E));
  DiodeBackward diodebackward_54 (.in(_74154_1_p23), .out(E));
  DiodeBackward diodebackward_55 (.in(_74154_1_p23), .out(D));
  DiodeBackward diodebackward_56 (.in(_74154_1_p24), .out(E));
  PullUp pullup_6 (.out(E));
  PullUp pullup_7 (.out(F));
  DiodeBackward diodebackward_57 (.in(_74154_1_p9), .out(F));
  DiodeBackward diodebackward_58 (.in(_74154_1_p13), .out(F));
  DiodeBackward diodebackward_59 (.in(_74154_1_p14), .out(F));
  DiodeBackward diodebackward_60 (.in(_74154_1_p15), .out(F));
  DiodeBackward diodebackward_61 (.in(_74154_1_p17), .out(F));
  DiodeBackward diodebackward_62 (.in(_74154_1_p18), .out(F));
  DiodeBackward diodebackward_63 (.in(_74154_1_p19), .out(F));
  DiodeBackward diodebackward_64 (.in(_74154_1_p20), .out(F));
  DiodeBackward diodebackward_65 (.in(_74154_1_p21), .out(F));
  DiodeBackward diodebackward_66 (.in(_74154_1_p23), .out(F));
  DiodeBackward diodebackward_67 (.in(_74154_1_p24), .out(F));
  PullUp pullup_8 (.out(G));
  DiodeBackward diodebackward_68 (.in(_74154_1_p11), .out(G));
  DiodeBackward diodebackward_69 (.in(_74154_1_p12), .out(G));
  DiodeBackward diodebackward_70 (.in(_74154_1_p13), .out(G));
  DiodeBackward diodebackward_71 (.in(_74154_1_p14), .out(G));
  DiodeBackward diodebackward_72 (.in(_74154_1_p15), .out(G));
  DiodeBackward diodebackward_73 (.in(_74154_1_p17), .out(G));
  DiodeBackward diodebackward_74 (.in(_74154_1_p18), .out(G));
  DiodeBackward diodebackward_75 (.in(_74154_1_p19), .out(G));
  DiodeBackward diodebackward_76 (.in(_74154_1_p20), .out(G));
  DiodeBackward diodebackward_77 (.in(_74154_1_p22), .out(G));
  DiodeBackward diodebackward_78 (.in(_74154_1_p23), .out(G));
  DiodeBackward diodebackward_79 (.in(_74154_1_p24), .out(G));
  Seven_Seg #(.commonCathode("true"), .commonConnectionType("anode")) seven_seg_1 (
    .a(A), .b(B), .c(C), .d(D), .e(E), .f(F), .g(G), .dp(dp), .common(1'b1));
endmodule
